# Fritzing sketch Schaltplan Raspberry (saved by Fritzing 0.9.3b)
breadboards: 1

parts:
  Rot = LEDs [package=led10mm]
  Grün = LEDs [package=led10mm]
  S1 = Pushbutton [package="[SMD]"]
  part = Raspberry Pi Zero
  Rot_2 = LEDs [package=led10mm]
  Gelb = LEDs [package=led10mm]
  Grün_2 = LEDs [package=led10mm]
  part_2 = Resistor [tolerance=±5% resistance=220 package="1206 [SMD]"]
  part_3 = Resistor [tolerance=±5% resistance=220 package="1206 [SMD]"]
  part_4 = Resistor [tolerance=±5% resistance=220 package="1206 [SMD]"]
  part_5 = Resistor [tolerance=±5% resistance=220 package="2512 [SMD]"]
  part_6 = Resistor [tolerance=±5% resistance=220 package="2512 [SMD]"]
  part_7 = Resistor [tolerance=±5% resistance=10k package="2512 [SMD]"]
  part_8 = Resistor [tolerance=±5% resistance=1k package="2512 [SMD]"]

nets:
  N1: Rot.C, part.pin_16
  N2: Rot.A, part_5.Pin_1
  N3: Grün.C, part.pin_18
  N4: Grün.A, part_6.Pin_1
  N5: S1.Pin_2, part.pin_22
  N6: S1.Pin_3, S1.Pin_4, part_7.Pin_1, part_8.Pin_1
  N7: part.pin_6, part.pin_14, part.pin_25, part.pin_39, part_2.Pin_0, part_3.Pin_0, part_4.Pin_0, part_5.Pin_0, part_6.Pin_0, part_7.Pin_0
  N8: part.pin_36, Rot_2.C
  N9: part.pin_37, part_8.Pin_0
  N10: part.pin_38, Gelb.C
  N11: part.pin_40, Grün_2.C
  N12: Rot_2.A, part_2.Pin_1
  N13: Gelb.A, part_3.Pin_1
  N14: Grün_2.A, part_4.Pin_1

// code stored in the sketch: Schaltplan.bas
import RPi.GPIO as gpio
import time
gpio.setmode(gpio.BOARD)
gpio.setup(36,gpio.OUT)
gpio.setup(38,gpio.OUT)
gpio.setup(40,gpio.OUT)
for i in range(3):
    gpio.output(36,gpio.HIGH)
    time.sleep(1)
    gpio.output(38,gpio.HIGH)
    time.sleep(1)
    gpio.output(36,gpio.LOW)
    gpio.output(38,gpio.LOW)
    gpio.output(40,gpio.HIGH)
    time.sleep(3)
    gpio.output(40,gpio.LOW)
    gpio.output(38,gpio.HIGH)
    time.sleep(1)
    gpio.output(38,gpio.LOW)
    gpio.output(36,gpio.HIGH)
    time.sleep(3)
gpio.cleanup()
